# Fritzing sketch Breath_scheme (saved by Fritzing 0.9.4)
breadboards: 1

parts:
  part = Arduino Nano (Rev3.0) (ICSP)
  Potentiometer = Trimmer Potentiometer [maximum_resistance=10kΩ package=THT]
  part_2 = LCD-16X2 [package=lcd-8x2]
  Alcohol_Sensor = IC, DIP package, 4 pins [chip_label=MQ-3]
  VCC1 = Battery block 9V
  S1 = Taiway 100-SP-X-T1 SPDT Miniature Toggle Switch [part_number="On/Off switch" package=THT]

nets:
  GND: part.GND, Potentiometer.leg1, part_2.VSS, part_2.R_W, Alcohol_Sensor.pin2, VCC1.-
  N1: part.D2, part_2.DB7
  N2: part.D3, part_2.DB6
  N3: part.D4, part_2.DB5
  N4: part.D5, part_2.DB4
  N5: part.VIN, S1.L2
  5V: part.5V, Potentiometer.leg2, part_2.VDD, Alcohol_Sensor.pin1
  N6: part.A5, Alcohol_Sensor.pin3
  N7: part.D12/MISO, part_2.RS
  N8: part.D11/MOSI, part_2.E
  N9: Potentiometer.wiper, part_2.VO
  N10: VCC1.+, S1.COM
